// Logisim project ex1.circ as structural Verilog: 1 circuit, main circuit generate_immediate
module generate_immediate (
  input  [31:0] INSTRUCTION,
  output [31:0] IMMEDIATE
);

  assign IMMEDIATE = {{20{INSTRUCTION[31]}}, {INSTRUCTION[31:25], INSTRUCTION[11:7]}};  // Bit_Extender bit_extender_1
  // also tied to GND on the sheet: {INSTRUCTION[0], INSTRUCTION[1], INSTRUCTION[2], INSTRUCTION[3], INSTRUCTION[4], INSTRUCTION[5], INSTRUCTION[6], INSTRUCTION[12], INSTRUCTION[13], INSTRUCTION[14], INSTRUCTION[15], INSTRUCTION[16], INSTRUCTION[17], INSTRUCTION[18], INSTRUCTION[19], INSTRUCTION[20], INSTRUCTION[21], INSTRUCTION[22], INSTRUCTION[23], INSTRUCTION[24]}

  // Other names for the same wires on the sheet: FIRST[4:0] = INSTRUCTION[11:7]; SECOND[6:0] = INSTRUCTION[31:25]
endmodule
